# Fritzing sketch receiver_328 (saved by Fritzing 0.9.2b)

parts:
  Part1 = Arduino Uno (Rev3)
  M1 = DC Motor
  S1 = H-Bridge with L298N
  VCC1 = Battery block 9V
  M2 = DC Motor
  M3 = DC Motor
  M4 = DC Motor

nets:
  N1: Part1.D9_PWM, S1.IN4
  GND: Part1.GND, S1.GND, VCC1.-
  N2: Part1.D3_PWM, S1.IN1
  N3: Part1.D5_PWM, S1.IN2
  N4: Part1.D6_PWM, S1.IN3
  5V: Part1.5V, S1.5V
  N5: M1.pin_1, S1.M2-02, M2.pin_1
  N6: M1.pin_2, S1.M2-01, M2.pin_2
  N7: S1.12V, VCC1.+
  N8: S1.ENA, S1.ENA-5V
  N9: S1.ENB, S1.ENB-5V
  N10: S1.M1-01, M3.pin_2, M4.pin_2
  N11: S1.M1-02, M3.pin_1, M4.pin_1

notes:
  pin lipo nha

custom parts:
  H-Bridge with L298N: h-bridge
