# Fritzing sketch tx_328 (saved by Fritzing 0.9.2b)
breadboards: 1

parts:
  Part1 = Arduino Uno (Rev3)
  S1 = Pushbutton [package="[SMD]"]
  S2 = Pushbutton [package="[SMD]"]
  S3 = Pushbutton [package="[SMD]"]
  S4 = Pushbutton [package="[SMD]"]
  LED1 = LED - 5mm [color="Red (633nm)" package="5 mm [THT]"]
  LED2 = LED - 5mm [color="Red (633nm)" package="5 mm [THT]"]
  LED3 = LED - 5mm [color="Red (633nm)" package="5 mm [THT]"]
  R1 = Resistor [tolerance=±5% resistance=220 package=THT]
  R2 = Resistor [tolerance=±5% resistance=220 package=THT]
  R3 = Resistor [tolerance=±5% resistance=220 package=THT]
  R4 = Resistor [tolerance=±5% resistance=220 package=THT]
  RE1 = Rotary Encoder [package=THT]

nets:
  N1: Part1.A0, RE1.EncoderPinC
  N2: Part1.D8, R3.Pin_1
  N3: Part1.GND, S1.Pin_3, S1.Pin_4, S2.Pin_3, S2.Pin_4, S3.Pin_3, S3.Pin_4, S4.Pin_3, S4.Pin_4, LED1.cathode, LED2.cathode, LED3.cathode, RE1.EncoderPinA
  N4: Part1.D2, S2.Pin_1, S2.Pin_2
  N5: Part1.D3_PWM, S1.Pin_1, S1.Pin_2
  N6: Part1.D4, S3.Pin_1, S3.Pin_2
  N7: Part1.D5_PWM, S4.Pin_1, S4.Pin_2
  N8: Part1.D6_PWM, R1.Pin_1
  N9: Part1.D7, R2.Pin_1
  N10: Part1.5V, R4.Pin_1
  N11: LED1.anode, R1.Pin_0
  N12: LED2.anode, R2.Pin_0
  N13: LED3.anode, R3.Pin_0
  N14: R4.Pin_0, RE1.EncoderPinB
